// Logisim project MIC-1-Grupo12marDesplazado.circ as structural Verilog
module main (
  input  CLK,
  output [31:0] PC,
  output [8:0] MPC,
  output [31:0] B,
  output [31:0] C
);

  wire control_unit_1_cpp_b, control_unit_1_cpp_c, control_unit_1_h_c, control_unit_1_lv_b,
       control_unit_1_lv_c, control_unit_1_mar_c, control_unit_1_mbr_b, control_unit_1_mbru_b,
       control_unit_1_mdr_b, control_unit_1_mdr_c, control_unit_1_opc_b, control_unit_1_opc_c,
       control_unit_1_pc_b, control_unit_1_pc_c, control_unit_1_sp_b, control_unit_1_sp_c,
       control_unit_1_tos_b, control_unit_1_tos_c, RESET_out, undriven, undriven_2;
  wire [1:0] control_unit_1_alu_2, control_unit_1_shifter;
  wire [2:0] control_unit_1_mem;
  wire [3:0] control_unit_1_alu;
  wire [7:0] data_path_1_op_code, mem_1_mem_fetch;
  wire [31:0] data_path_1_mem_mar, data_path_1_mem_wr, mem_1_mrm_rd;

  Mem mem_1 (
    .MEM_ADDR_32(data_path_1_mem_mar), .CLK(CLK), .MEM_WR(data_path_1_mem_wr), .MRM_RD(mem_1_mrm_rd),
    .MEM_FETCH(mem_1_mem_fetch), .wr(control_unit_1_mem[2]), .rd(control_unit_1_mem[1]),
    .fetch(control_unit_1_mem[0]), .MEM_ADDR_8(PC));
  Button RESET (.out(RESET_out));
  Data_Path data_path_1 (
    .MEM_WR(data_path_1_mem_wr), .MEM_RD(mem_1_mrm_rd), .rd(control_unit_1_mem[1]),
    .MEM_FETCH(mem_1_mem_fetch), .RESET(RESET_out), .INVA(control_unit_1_alu[1]),
    .ENA(control_unit_1_alu[3]), .CLK(CLK), .ENB(control_unit_1_alu[2]), .INC(control_unit_1_alu[0]),
    .F(control_unit_1_alu_2), .SRA1(control_unit_1_shifter[0]), .SLL8(control_unit_1_shifter[1]),
    .MEM_MAR(data_path_1_mem_mar), .OP_CODE(data_path_1_op_code), .MAR_C(control_unit_1_mar_c),
    .MDR_C(control_unit_1_mdr_c), .PC_C(control_unit_1_pc_c), .fetch(control_unit_1_mem[0]),
    .SP_C(control_unit_1_sp_c), .LV_C(control_unit_1_lv_c), .CPP_C(control_unit_1_cpp_c),
    .TOS_C(control_unit_1_tos_c), .OPC_C(control_unit_1_opc_c), .H_C(control_unit_1_h_c),
    .MBR(control_unit_1_mbr_b), .MBRU(control_unit_1_mbru_b), .MDR_B(control_unit_1_mdr_b),
    .PC_B(control_unit_1_pc_b), .SP_B(control_unit_1_sp_b), .LV_B(control_unit_1_lv_b),
    .CPP_B(control_unit_1_cpp_b), .TOS_B(control_unit_1_tos_b), .OPC_B(control_unit_1_opc_b), .MEM_PC(PC),
    .B(B), .C(C));  // open: N, Z
  Control_Unit control_unit_1 (
    .CLK(CLK), .RESET(RESET_out), .MBR(data_path_1_op_code), .N(undriven), .Z(undriven_2), .MPC(MPC),
    .MDR_B(control_unit_1_mdr_b), .PC_B(control_unit_1_pc_b), .MBR_B(control_unit_1_mbr_b),
    .MBRU_B(control_unit_1_mbru_b), .SP_B(control_unit_1_sp_b), .LV_B(control_unit_1_lv_b),
    .CPP_B(control_unit_1_cpp_b), .TOS_B(control_unit_1_tos_b), .OPC_B(control_unit_1_opc_b),
    .Mem(control_unit_1_mem), .ALU({control_unit_1_alu_2, control_unit_1_alu}),
    .Shifter(control_unit_1_shifter), .H_C(control_unit_1_h_c), .OPC_C(control_unit_1_opc_c),
    .TOS_C(control_unit_1_tos_c), .CPP_C(control_unit_1_cpp_c), .LV_C(control_unit_1_lv_c),
    .SP_C(control_unit_1_sp_c), .PC_C(control_unit_1_pc_c), .MDR_C(control_unit_1_mdr_c),
    .MAR_C(control_unit_1_mar_c));
endmodule

module Mem (
  input  wr,
  input  [31:0] MEM_WR,
  input  [31:0] MEM_ADDR_32,
  input  rd,
  input  [31:0] MEM_ADDR_8,
  input  fetch,
  input  CLK,
  output [31:0] MRM_RD,
  output [7:0] MEM_FETCH
);

  wire not_1_out, not_2_out, not_3_out;
  wire [7:0] ram_2_data;
  wire [31:0] ram_1_data;

  not not_1 (not_1_out, CLK);
  not not_2 (not_2_out, wr);
  RAM #(.addrWidth(24), .dataWidth(32)) ram_1 (
    .addr(MEM_ADDR_32[23:0]), .data(ram_1_data), .sel(1'b1), .clk(not_1_out), .ld(not_2_out), .clr(1'b0));
  assign ram_1_data = wr ? MEM_WR : 32'bz;  // Controlled_Buffer controlled_buffer_1
  assign MRM_RD = rd ? ram_1_data : 32'bz;  // Controlled_Buffer controlled_buffer_2
  not not_3 (not_3_out, CLK);
  assign MEM_FETCH = fetch ? ram_2_data : 8'bz;  // Controlled_Buffer controlled_buffer_3
  RAM #(.addrWidth(24)) ram_2 (
    .addr(MEM_ADDR_8[23:0]), .data(ram_2_data), .sel(1'b1), .clk(not_3_out), .clr(1'b0));  // open: ld

  // Notes on the sheet:
  //   Una truchada porque Logisim no tiene
  //   un bloque de memoria con dos canales de datos
endmodule

module Control_Unit (
  input  CLK,
  input  RESET,
  input  [7:0] MBR,
  input  N,
  input  Z,
  output [8:0] MPC,
  output MDR_B,
  output PC_B,
  output MBR_B,
  output MBRU_B,
  output SP_B,
  output LV_B,
  output CPP_B,
  output TOS_B,
  output OPC_B,
  output [2:0] Mem,
  output [5:0] ALU,
  output [1:0] Shifter,
  output H_C,
  output OPC_C,
  output TOS_C,
  output CPP_C,
  output LV_C,
  output SP_C,
  output PC_C,
  output MDR_C,
  output MAR_C
);

  wire and_1_out, and_2_out, d_flipflop_asc_1_q, d_flipflop_asc_2_q, not_1_out;
  wire [2:0] mir_1_jam;
  wire [3:0] control_store_1_cs_s4, mir_1_b;
  wire [7:0] mir_1_addr, multiplexer_3_out, or_2_out;
  wire [8:0] multiplexer_1_out, multiplexer_2_out;
  wire [8:8] mir_1_addr_2, or_1_out;
  wire [31:0] control_store_1_cs_s32;

  Multiplexer #(.width(9), .enable("false")) multiplexer_1 (
    .in0({9{1'b1}}), .in1(9'hff), .out(multiplexer_1_out), .sel(RESET));
  Multiplexer #(.width(9), .enable("false")) multiplexer_2 (
    .in0({9{1'b1}}), .in1(9'h100), .out(multiplexer_2_out), .sel(RESET));
  and and_1 (and_1_out, d_flipflop_asc_1_q, mir_1_jam[1]);
  D_FlipFlop_Asc d_flipflop_asc_1 (
    .D(N), .CLK(CLK), .Q(d_flipflop_asc_1_q), .nPRE(1'b1), .nCLR(not_1_out));  // open: nQ
  D_FlipFlop_Asc d_flipflop_asc_2 (
    .D(Z), .CLK(CLK), .Q(d_flipflop_asc_2_q), .nPRE(1'b1), .nCLR(not_1_out));  // open: nQ
  Multiplexer #(.width(8), .enable("false")) multiplexer_3 (
    .in0(mir_1_addr), .in1(or_2_out), .out(multiplexer_3_out), .sel(mir_1_jam[2]));
  or or_1 (or_1_out[8], and_1_out, and_2_out, mir_1_addr_2[8]);
  and and_2 (and_2_out, d_flipflop_asc_2_q, mir_1_jam[0]);
  assign or_2_out = MBR | mir_1_addr;  // OR_Gate or_2, 8 bits wide
  not not_1 (not_1_out, RESET);
  MPC mpc_1 (
    .Entrada({or_1_out[8], multiplexer_3_out}), .CLK(CLK), .Salida(MPC), .nPRE(multiplexer_1_out),
    .nCLR(multiplexer_2_out));
  Control_Store control_store_1 (.CS_E(MPC), .CS_S32(control_store_1_cs_s32), .CS_S4(control_store_1_cs_s4));
  MIR mir_1 (
    .Entrada_4(control_store_1_cs_s4), .Entrada_32(control_store_1_cs_s32), .CLK(CLK), .RESET(RESET),
    .B(mir_1_b), .Mem(Mem), .C({H_C, OPC_C, TOS_C, CPP_C, LV_C, SP_C, PC_C, MDR_C, MAR_C}),
    .ALU({Shifter, ALU}), .JAM(mir_1_jam), .Addr({mir_1_addr_2[8], mir_1_addr}));
  Decoder #(.select(4), .enable("false")) decoder_1 (
    .out0(MDR_B), .out1(PC_B), .out2(MBR_B), .out3(MBRU_B), .out4(SP_B), .out5(LV_B), .out6(CPP_B),
    .out7(TOS_B), .out8(OPC_B), .sel(mir_1_b));  // open: out9, out10, out11, out12, out13, out14, out15
endmodule

module Control_Store (
  input  [8:0] CS_E,
  output [31:0] CS_S32,
  output [3:0] CS_S4
);

  ROM #(.addrWidth(9), .dataWidth(32)) rom_1 (.addr(CS_E), .data(CS_S32), .sel(1'b1));
  ROM #(.addrWidth(9), .dataWidth(4)) rom_2 (.addr(CS_E), .data(CS_S4), .sel(1'b1));

  // Notes on the sheet:
  //   Otra truchada porque Logisim no tiene
  //   un bloque de memoria mas ancho que 32 bits
  //   contents of rom_1 (hex, n*v repeats v):
  //   80000000 255*0 435021
  //   contents of rom_2 (hex, n*v repeats v):
  //   f 255*0 1
endmodule

module MPC (
  input  [8:0] nPRE,
  input  [8:0] Entrada,
  input  CLK,
  input  [8:0] nCLR,
  output [8:0] Salida
);

  D_Latch d_latch_1 (.D(Entrada[8]), .CLK(CLK), .Q(Salida[8]), .nPRE(nPRE[8]), .nCLR(nCLR[8]));  // open: nQ
  D_Latch d_latch_2 (.D(Entrada[7]), .CLK(CLK), .Q(Salida[7]), .nPRE(nPRE[7]), .nCLR(nCLR[7]));  // open: nQ
  D_Latch d_latch_3 (.D(Entrada[6]), .CLK(CLK), .Q(Salida[6]), .nPRE(nPRE[6]), .nCLR(nCLR[6]));  // open: nQ
  D_Latch d_latch_4 (.D(Entrada[5]), .CLK(CLK), .Q(Salida[5]), .nPRE(nPRE[5]), .nCLR(nCLR[5]));  // open: nQ
  D_Latch d_latch_5 (.D(Entrada[4]), .CLK(CLK), .Q(Salida[4]), .nPRE(nPRE[4]), .nCLR(nCLR[4]));  // open: nQ
  D_Latch d_latch_6 (.D(Entrada[3]), .CLK(CLK), .Q(Salida[3]), .nPRE(nPRE[3]), .nCLR(nCLR[3]));  // open: nQ
  D_Latch d_latch_7 (.D(Entrada[2]), .CLK(CLK), .Q(Salida[2]), .nPRE(nPRE[2]), .nCLR(nCLR[2]));  // open: nQ
  D_Latch d_latch_8 (.D(Entrada[1]), .CLK(CLK), .Q(Salida[1]), .nPRE(nPRE[1]), .nCLR(nCLR[1]));  // open: nQ
  D_Latch d_latch_9 (.D(Entrada[0]), .CLK(CLK), .Q(Salida[0]), .nPRE(nPRE[0]), .nCLR(nCLR[0]));  // open: nQ
endmodule

module MIR (
  input  [3:0] Entrada_4,
  input  [31:0] Entrada_32,
  input  CLK,
  input  RESET,
  output [3:0] B,
  output [2:0] Mem,
  output [8:0] C,
  output [7:0] ALU,
  output [2:0] JAM,
  output [8:0] Addr
);

  wire [3:0] multiplexer_2_out, multiplexer_4_out, not_2_out;
  wire [31:0] multiplexer_1_out, multiplexer_3_out, not_1_out;

  Multiplexer #(.width(32), .enable("false")) multiplexer_1 (
    .in0({32{1'b1}}), .in1(not_1_out), .out(multiplexer_1_out), .sel(RESET));
  assign not_1_out = ~32'h435021;  // NOT_Gate not_1, 32 bits wide
  assign not_2_out = ~4'b0001;  // NOT_Gate not_2, 4 bits wide
  Multiplexer #(.width(4), .enable("false")) multiplexer_2 (
    .in0(4'b1111), .in1(not_2_out), .out(multiplexer_2_out), .sel(RESET));
  Multiplexer #(.width(32), .enable("false")) multiplexer_3 (
    .in0({32{1'b1}}), .in1(32'h435021), .out(multiplexer_3_out), .sel(RESET));
  Multiplexer #(.width(4), .enable("false")) multiplexer_4 (
    .in0(4'b1111), .in1(4'b0001), .out(multiplexer_4_out), .sel(RESET));
  Register_32_bits_Des register_32_bits_des_1 (
    .Entrada(Entrada_32), .CLK(CLK), .Salida({Addr, JAM, ALU, C, Mem}), .nPRE(multiplexer_1_out),
    .nCLR(multiplexer_3_out));
  Register_4_bits_Des register_4_bits_des_1 (
    .Entrada(Entrada_4), .CLK(CLK), .Salida(B), .nPRE(multiplexer_2_out), .nCLR(multiplexer_4_out));
endmodule

module Data_Path (
  input  MAR_C,
  input  [31:0] MEM_RD,
  input  MDR_B,
  input  MDR_C,
  input  rd,
  input  [7:0] MEM_FETCH,
  input  PC_B,
  input  PC_C,
  input  MBR,
  input  fetch,
  input  MBRU,
  input  SP_B,
  input  SP_C,
  input  LV_B,
  input  LV_C,
  input  CPP_B,
  input  CPP_C,
  input  TOS_B,
  input  RESET,
  input  TOS_C,
  input  OPC_B,
  input  OPC_C,
  input  H_C,
  input  INVA,
  input  ENA,
  input  CLK,
  input  ENB,
  input  INC,
  input  [1:0] F,
  input  SRA1,
  input  SLL8,
  output [31:0] MEM_MAR,
  output [31:0] MEM_WR,
  output [31:0] MEM_PC,
  output [7:0] OP_CODE,
  output [31:0] B,
  output N,
  output Z,
  output [31:0] C
);

  wire [7:0] multiplexer_1_out;
  wire [31:0] alu_32_bits_1_s, multiplexer_2_out, multiplexer_3_out,
       register_32_bits_hold_paralel_load_1_salida, register_32_bits_hold_paralel_load_4_salida,
       register_32_bits_hold_paralel_load_5_salida, register_32_bits_hold_paralel_load_6_salida,
       register_32_bits_hold_paralel_load_7_salida, register_32_bits_hold_paralel_load_8_salida,
       register_32_bits_hold_paralel_load_9_salida;

  Multiplexer #(.width(8), .enable("false")) multiplexer_1 (
    .in0({8{1'b1}}), .in1({8{1'b0}}), .out(multiplexer_1_out), .sel(RESET));
  Multiplexer #(.width(32), .enable("false")) multiplexer_2 (
    .in0({32{1'b1}}), .in1({32{1'b0}}), .out(multiplexer_2_out), .sel(RESET));
  Multiplexer #(.width(32), .enable("false")) multiplexer_3 (.in0(C), .in1(MEM_RD), .out(multiplexer_3_out), .sel(rd));
  Register_8_bits_Hold___Paralel_Load register_8_bits_hold_paralel_load_1 (
    .Entrada(MEM_FETCH), .LOAD(fetch), .CLK(CLK), .Salida(OP_CODE), .nPRE({8{1'b1}}), .nCLR(multiplexer_1_out));
  Register_32_bits_Hold___Paralel_Load register_32_bits_hold_paralel_load_1 (
    .Entrada(C), .LOAD(MAR_C), .CLK(CLK), .Salida(register_32_bits_hold_paralel_load_1_salida),
    .nPRE({32{1'b1}}), .nCLR(multiplexer_2_out));
  assign B = MDR_B ? MEM_WR : 32'bz;  // Controlled_Buffer controlled_buffer_1
  Register_32_bits_Hold___Paralel_Load register_32_bits_hold_paralel_load_2 (
    .Entrada(multiplexer_3_out), .LOAD(MDR_C), .CLK(CLK), .Salida(MEM_WR), .nPRE({32{1'b1}}),
    .nCLR(multiplexer_2_out));
  Register_32_bits_Hold___Paralel_Load register_32_bits_hold_paralel_load_3 (
    .Entrada(C), .LOAD(PC_C), .CLK(CLK), .Salida(MEM_PC), .nPRE({32{1'b1}}), .nCLR(multiplexer_2_out));
  assign B = PC_B ? MEM_PC : 32'bz;  // Controlled_Buffer controlled_buffer_2
  MBR_EN mbr_en_1 (.in_1(OP_CODE), .Salida_Signada(B), .Salida_No_Signada(B), .MRB(MBR), .MBRU(MBRU));
  Register_32_bits_Hold___Paralel_Load register_32_bits_hold_paralel_load_4 (
    .Entrada(C), .LOAD(SP_C), .CLK(CLK), .Salida(register_32_bits_hold_paralel_load_4_salida),
    .nPRE({32{1'b1}}), .nCLR(multiplexer_2_out));
  assign B = SP_B ? register_32_bits_hold_paralel_load_4_salida : 32'bz;  // Controlled_Buffer controlled_buffer_3
  Register_32_bits_Hold___Paralel_Load register_32_bits_hold_paralel_load_5 (
    .Entrada(C), .LOAD(LV_C), .CLK(CLK), .Salida(register_32_bits_hold_paralel_load_5_salida),
    .nPRE({32{1'b1}}), .nCLR(multiplexer_2_out));
  assign B = LV_B ? register_32_bits_hold_paralel_load_5_salida : 32'bz;  // Controlled_Buffer controlled_buffer_4
  assign B = CPP_B ? register_32_bits_hold_paralel_load_6_salida : 32'bz;  // Controlled_Buffer controlled_buffer_5
  Register_32_bits_Hold___Paralel_Load register_32_bits_hold_paralel_load_6 (
    .Entrada(C), .LOAD(CPP_C), .CLK(CLK), .Salida(register_32_bits_hold_paralel_load_6_salida),
    .nPRE({32{1'b1}}), .nCLR(multiplexer_2_out));
  Register_32_bits_Hold___Paralel_Load register_32_bits_hold_paralel_load_7 (
    .Entrada(C), .LOAD(TOS_C), .CLK(CLK), .Salida(register_32_bits_hold_paralel_load_7_salida),
    .nPRE({32{1'b1}}), .nCLR(multiplexer_2_out));
  assign B = TOS_B ? register_32_bits_hold_paralel_load_7_salida : 32'bz;  // Controlled_Buffer controlled_buffer_6
  Register_32_bits_Hold___Paralel_Load register_32_bits_hold_paralel_load_8 (
    .Entrada(C), .LOAD(OPC_C), .CLK(CLK), .Salida(register_32_bits_hold_paralel_load_8_salida),
    .nPRE({32{1'b1}}), .nCLR(multiplexer_2_out));
  assign B = OPC_B ? register_32_bits_hold_paralel_load_8_salida : 32'bz;  // Controlled_Buffer controlled_buffer_7
  Register_32_bits_Hold___Paralel_Load register_32_bits_hold_paralel_load_9 (
    .Entrada(C), .LOAD(H_C), .CLK(CLK), .Salida(register_32_bits_hold_paralel_load_9_salida),
    .nPRE({32{1'b1}}), .nCLR(multiplexer_2_out));
  Shifter #(.width(32)) shifter_1 (.in(register_32_bits_hold_paralel_load_1_salida), .\dist (5'b00010), .out(MEM_MAR));
  Desplazador desplazador_1 (.SRA1(SRA1), .Entrada(alu_32_bits_1_s), .Salida(C), .SLL8(SLL8));
  ALU_32_Bits alu_32_bits_1 (
    .A(register_32_bits_hold_paralel_load_9_salida), .ENB(ENB), .ENA(ENA), .INA(INVA), .B(B), .in_7(F),
    .S(alu_32_bits_1_s), .CIN(INC));  // open: COUT
  ZN zn_1 (.in_1(alu_32_bits_1_s), .Z(Z), .N(N));

  // Notes on the sheet:
  //   Preset 8 Bits
  //   Clear 8 Bits
  //   Preset 32 Bits
  //   Clear 32 Bits
  //   Bus B
  //   Bus C
  //   N: Extrae el bit mas significativo para el signo
  //   Z: Se fija si la salida de la ALU == 0
endmodule

module Register_32_bits_Hold___Paralel_Load (
  input  [31:0] nPRE,
  input  [31:0] Entrada,
  input  [31:0] nCLR,
  input  LOAD,
  input  CLK,
  output [31:0] Salida
);

  wire [31:0] multiplexer_1_out;

  Multiplexer #(.width(32), .enable("false")) multiplexer_1 (
    .in1(Entrada), .out(multiplexer_1_out), .sel(LOAD));  // open: in0
  Register_32_bits_Des register_32_bits_des_1 (
    .Entrada(multiplexer_1_out), .CLK(CLK), .Salida(Salida), .nPRE(nPRE), .nCLR(nCLR));
endmodule

module Register_32_bits_Des (
  input  [31:0] nPRE,
  input  [31:0] Entrada,
  input  CLK,
  input  [31:0] nCLR,
  output [31:0] Salida
);

  D_FlipFlop_Des d_flipflop_des_1 (
    .D(Entrada[31]), .CLK(CLK), .Q(Salida[31]), .nPRE(nPRE[31]), .nCLR(nCLR[31]));  // open: nQ
  D_FlipFlop_Des d_flipflop_des_2 (
    .D(Entrada[30]), .CLK(CLK), .Q(Salida[30]), .nPRE(nPRE[30]), .nCLR(nCLR[30]));  // open: nQ
  D_FlipFlop_Des d_flipflop_des_3 (
    .D(Entrada[29]), .CLK(CLK), .Q(Salida[29]), .nPRE(nPRE[29]), .nCLR(nCLR[29]));  // open: nQ
  D_FlipFlop_Des d_flipflop_des_4 (
    .D(Entrada[28]), .CLK(CLK), .Q(Salida[28]), .nPRE(nPRE[28]), .nCLR(nCLR[28]));  // open: nQ
  D_FlipFlop_Des d_flipflop_des_5 (
    .D(Entrada[27]), .CLK(CLK), .Q(Salida[27]), .nPRE(nPRE[27]), .nCLR(nCLR[27]));  // open: nQ
  D_FlipFlop_Des d_flipflop_des_6 (
    .D(Entrada[26]), .CLK(CLK), .Q(Salida[26]), .nPRE(nPRE[26]), .nCLR(nCLR[26]));  // open: nQ
  D_FlipFlop_Des d_flipflop_des_7 (
    .D(Entrada[25]), .CLK(CLK), .Q(Salida[25]), .nPRE(nPRE[25]), .nCLR(nCLR[25]));  // open: nQ
  D_FlipFlop_Des d_flipflop_des_8 (
    .D(Entrada[24]), .CLK(CLK), .Q(Salida[24]), .nPRE(nPRE[24]), .nCLR(nCLR[24]));  // open: nQ
  D_FlipFlop_Des d_flipflop_des_9 (
    .D(Entrada[23]), .CLK(CLK), .Q(Salida[23]), .nPRE(nPRE[23]), .nCLR(nCLR[23]));  // open: nQ
  D_FlipFlop_Des d_flipflop_des_10 (
    .D(Entrada[22]), .CLK(CLK), .Q(Salida[22]), .nPRE(nPRE[22]), .nCLR(nCLR[22]));  // open: nQ
  D_FlipFlop_Des d_flipflop_des_11 (
    .D(Entrada[21]), .CLK(CLK), .Q(Salida[21]), .nPRE(nPRE[21]), .nCLR(nCLR[21]));  // open: nQ
  D_FlipFlop_Des d_flipflop_des_12 (
    .D(Entrada[20]), .CLK(CLK), .Q(Salida[20]), .nPRE(nPRE[20]), .nCLR(nCLR[20]));  // open: nQ
  D_FlipFlop_Des d_flipflop_des_13 (
    .D(Entrada[19]), .CLK(CLK), .Q(Salida[19]), .nPRE(nPRE[19]), .nCLR(nCLR[19]));  // open: nQ
  D_FlipFlop_Des d_flipflop_des_14 (
    .D(Entrada[18]), .CLK(CLK), .Q(Salida[18]), .nPRE(nPRE[18]), .nCLR(nCLR[18]));  // open: nQ
  D_FlipFlop_Des d_flipflop_des_15 (
    .D(Entrada[17]), .CLK(CLK), .Q(Salida[17]), .nPRE(nPRE[17]), .nCLR(nCLR[17]));  // open: nQ
  D_FlipFlop_Des d_flipflop_des_16 (
    .D(Entrada[16]), .CLK(CLK), .Q(Salida[16]), .nPRE(nPRE[16]), .nCLR(nCLR[16]));  // open: nQ
  D_FlipFlop_Des d_flipflop_des_17 (
    .D(Entrada[15]), .CLK(CLK), .Q(Salida[15]), .nPRE(nPRE[15]), .nCLR(nCLR[15]));  // open: nQ
  D_FlipFlop_Des d_flipflop_des_18 (
    .D(Entrada[14]), .CLK(CLK), .Q(Salida[14]), .nPRE(nPRE[14]), .nCLR(nCLR[14]));  // open: nQ
  D_FlipFlop_Des d_flipflop_des_19 (
    .D(Entrada[13]), .CLK(CLK), .Q(Salida[13]), .nPRE(nPRE[13]), .nCLR(nCLR[13]));  // open: nQ
  D_FlipFlop_Des d_flipflop_des_20 (
    .D(Entrada[12]), .CLK(CLK), .Q(Salida[12]), .nPRE(nPRE[12]), .nCLR(nCLR[12]));  // open: nQ
  D_FlipFlop_Des d_flipflop_des_21 (
    .D(Entrada[11]), .CLK(CLK), .Q(Salida[11]), .nPRE(nPRE[11]), .nCLR(nCLR[11]));  // open: nQ
  D_FlipFlop_Des d_flipflop_des_22 (
    .D(Entrada[10]), .CLK(CLK), .Q(Salida[10]), .nPRE(nPRE[10]), .nCLR(nCLR[10]));  // open: nQ
  D_FlipFlop_Des d_flipflop_des_23 (
    .D(Entrada[9]), .CLK(CLK), .Q(Salida[9]), .nPRE(nPRE[9]), .nCLR(nCLR[9]));  // open: nQ
  D_FlipFlop_Des d_flipflop_des_24 (
    .D(Entrada[8]), .CLK(CLK), .Q(Salida[8]), .nPRE(nPRE[8]), .nCLR(nCLR[8]));  // open: nQ
  D_FlipFlop_Des d_flipflop_des_25 (
    .D(Entrada[7]), .CLK(CLK), .Q(Salida[7]), .nPRE(nPRE[7]), .nCLR(nCLR[7]));  // open: nQ
  D_FlipFlop_Des d_flipflop_des_26 (
    .D(Entrada[6]), .CLK(CLK), .Q(Salida[6]), .nPRE(nPRE[6]), .nCLR(nCLR[6]));  // open: nQ
  D_FlipFlop_Des d_flipflop_des_27 (
    .D(Entrada[5]), .CLK(CLK), .Q(Salida[5]), .nPRE(nPRE[5]), .nCLR(nCLR[5]));  // open: nQ
  D_FlipFlop_Des d_flipflop_des_28 (
    .D(Entrada[4]), .CLK(CLK), .Q(Salida[4]), .nPRE(nPRE[4]), .nCLR(nCLR[4]));  // open: nQ
  D_FlipFlop_Des d_flipflop_des_29 (
    .D(Entrada[3]), .CLK(CLK), .Q(Salida[3]), .nPRE(nPRE[3]), .nCLR(nCLR[3]));  // open: nQ
  D_FlipFlop_Des d_flipflop_des_30 (
    .D(Entrada[2]), .CLK(CLK), .Q(Salida[2]), .nPRE(nPRE[2]), .nCLR(nCLR[2]));  // open: nQ
  D_FlipFlop_Des d_flipflop_des_31 (
    .D(Entrada[1]), .CLK(CLK), .Q(Salida[1]), .nPRE(nPRE[1]), .nCLR(nCLR[1]));  // open: nQ
  D_FlipFlop_Des d_flipflop_des_32 (
    .D(Entrada[0]), .CLK(CLK), .Q(Salida[0]), .nPRE(nPRE[0]), .nCLR(nCLR[0]));  // open: nQ
endmodule

module Register_8_bits_Hold___Paralel_Load (
  input  [7:0] nPRE,
  input  [7:0] Entrada,
  input  LOAD,
  input  CLK,
  input  [7:0] nCLR,
  output [7:0] Salida
);

  wire [7:0] multiplexer_1_out;

  Multiplexer #(.width(8), .enable("false")) multiplexer_1 (
    .in1(Entrada), .out(multiplexer_1_out), .sel(LOAD));  // open: in0
  Register_4_bits_Des register_4_bits_des_1 (
    .Entrada(multiplexer_1_out[7:4]), .CLK(CLK), .Salida(Salida[7:4]), .nPRE(nPRE[7:4]), .nCLR(nCLR[7:4]));
  Register_4_bits_Des register_4_bits_des_2 (
    .Entrada(multiplexer_1_out[3:0]), .CLK(CLK), .Salida(Salida[3:0]), .nPRE(nPRE[3:0]), .nCLR(nCLR[3:0]));
endmodule

module Register_4_bits_Des (
  input  [3:0] nPRE,
  input  [3:0] Entrada,
  input  CLK,
  input  [3:0] nCLR,
  output [3:0] Salida
);

  D_FlipFlop_Des d_flipflop_des_1 (
    .D(Entrada[3]), .CLK(CLK), .Q(Salida[3]), .nPRE(nPRE[3]), .nCLR(nCLR[3]));  // open: nQ
  D_FlipFlop_Des d_flipflop_des_2 (
    .D(Entrada[2]), .CLK(CLK), .Q(Salida[2]), .nPRE(nPRE[2]), .nCLR(nCLR[2]));  // open: nQ
  D_FlipFlop_Des d_flipflop_des_3 (
    .D(Entrada[1]), .CLK(CLK), .Q(Salida[1]), .nPRE(nPRE[1]), .nCLR(nCLR[1]));  // open: nQ
  D_FlipFlop_Des d_flipflop_des_4 (
    .D(Entrada[0]), .CLK(CLK), .Q(Salida[0]), .nPRE(nPRE[0]), .nCLR(nCLR[0]));  // open: nQ
endmodule

module MBR_EN (
  input  [7:0] in_1,
  input  MRB,
  input  MBRU,
  output [31:0] Salida_Signada,
  output [31:0] Salida_No_Signada
);

  assign Salida_Signada = MRB ? {{25{in_1[7]}}, in_1[6:0]} : 32'bz;  // Controlled_Buffer controlled_buffer_1
  assign Salida_No_Signada = MBRU ? {{24{1'b0}}, in_1} : 32'bz;  // Controlled_Buffer controlled_buffer_2
endmodule

module D_FlipFlop_Des (
  input  nPRE,
  input  D,
  input  CLK,
  input  nCLR,
  output Q,
  output nQ
);

  wire d_latch_1_q, not_1_out;

  not not_1 (not_1_out, CLK);
  D_Latch d_latch_1 (.D(D), .CLK(CLK), .Q(d_latch_1_q), .nPRE(nPRE), .nCLR(nCLR));  // open: nQ
  D_Latch d_latch_2 (.D(d_latch_1_q), .CLK(not_1_out), .Q(Q), .nQ(nQ), .nPRE(nPRE), .nCLR(nCLR));
endmodule

module D_FlipFlop_Asc (
  input  nPRE,
  input  D,
  input  CLK,
  input  nCLR,
  output Q,
  output nQ
);

  wire d_latch_1_q, not_1_out;

  not not_1 (not_1_out, CLK);
  D_Latch d_latch_1 (.D(D), .CLK(not_1_out), .Q(d_latch_1_q), .nPRE(nPRE), .nCLR(nCLR));  // open: nQ
  D_Latch d_latch_2 (.D(d_latch_1_q), .CLK(CLK), .Q(Q), .nQ(nQ), .nPRE(nPRE), .nCLR(nCLR));
endmodule

module D_Latch (
  input  nPRE,
  input  D,
  input  CLK,
  input  nCLR,
  output Q,
  output nQ
);

  wire and_1_out, and_2_out, nand_1_out, nand_2_out, not_1_out;

  not not_1 (not_1_out, D);
  nand nand_1 (nand_1_out, D, CLK);
  nand nand_2 (nand_2_out, CLK, not_1_out);
  and and_1 (and_1_out, nPRE, nand_1_out);
  nand nand_3 (Q, and_1_out, nQ);
  nand nand_4 (nQ, Q, and_2_out);
  and and_2 (and_2_out, nand_2_out, nCLR);
endmodule

module ALU_1_bit (
  input  Cin,
  input  INVA,
  input  A,
  input  ENA,
  input  B,
  input  ENB,
  input  [1:0] F,
  output Salida,
  output Cout
);

  wire and_1_out, and_2_out, and_3_out, and_4_out, and_5_out, and_6_out, sumador_completo_alu_1_s,
       unidad_logica_alu_1_and, unidad_logica_alu_1_not, unidad_logica_alu_1_or, xor_1_out;

  xor xor_1 (xor_1_out, INVA, and_1_out);
  and and_1 (and_1_out, A, ENA);
  and and_2 (and_2_out, B, ENB);
  and and_3 (and_3_out, ~F[0], ~F[1]);  // AND_Gate
  and and_4 (and_4_out, ~F[0], F[1]);  // AND_Gate
  and and_5 (and_5_out, F[0], ~F[1]);  // AND_Gate
  and and_6 (and_6_out, F[0], F[1]);
  Unidad_Logica__ALU unidad_logica_alu_1 (
    .A(xor_1_out), .B(and_2_out), .EN1(and_3_out), .EN2(and_4_out), .EN3(and_5_out),
    .AND(unidad_logica_alu_1_and), .OR(unidad_logica_alu_1_or), .NOT(unidad_logica_alu_1_not));
  Sumador_Completo__ALU sumador_completo_alu_1 (
    .A(xor_1_out), .B(and_2_out), .EN(and_6_out), .S(sumador_completo_alu_1_s), .Cin(Cin), .Cout(Cout));
  or or_1 (Salida, unidad_logica_alu_1_and, unidad_logica_alu_1_or, unidad_logica_alu_1_not, sumador_completo_alu_1_s);
endmodule

module Unidad_Logica__ALU (
  input  A,
  input  B,
  input  EN1,
  input  EN2,
  input  EN3,
  output AND,
  output OR,
  output NOT
);

  wire and_1_out, not_1_out, or_1_out;

  and and_1 (and_1_out, A, B);
  or or_1 (or_1_out, A, B);
  not not_1 (not_1_out, A);
  and and_2 (AND, and_1_out, EN1);
  and and_3 (OR, or_1_out, EN2);
  and and_4 (NOT, not_1_out, EN3);
endmodule

module Sumador_Completo__ALU (
  input  Cin,
  input  A,
  input  B,
  input  EN,
  output S,
  output Cout
);

  wire and_1_out, and_2_out, xor_1_out, xor_2_out;

  and and_1 (and_1_out, A, B, EN);
  xor xor_1 (xor_1_out, A, B);
  and and_2 (and_2_out, Cin, xor_1_out, EN);
  or or_1 (Cout, and_1_out, and_2_out);
  xor xor_2 (xor_2_out, Cin, xor_1_out);
  and and_3 (S, xor_2_out, EN);
endmodule

module Desplazador (
  input  [31:0] Entrada,
  input  SRA1,
  input  SLL8,
  output [31:0] Salida
);

  wire and_1_out, and_2_out, and_3_out, and_4_out, and_5_out, and_6_out, and_7_out, and_8_out, and_9_out,
       and_10_out, and_12_out, and_15_out, and_17_out, and_18_out, and_20_out, and_22_out, and_24_out,
       and_27_out, and_28_out, and_30_out, and_33_out, and_35_out, and_37_out, and_38_out, LA, LB, LC, LD,
       LE, LF, LG, LH, LI, LJ, LK, LL, LM, LN, LO, LP, LQ, LR, LS, LT, LU, LV, LW, LX;

  and and_1 (and_1_out, SRA1, Entrada[31]);
  and and_2 (and_2_out, Entrada[31], SRA1);
  or or_1 (Salida[31], and_1_out, LA);
  and and_3 (and_3_out, Entrada[30], SRA1);
  or or_2 (Salida[30], and_2_out, LB);
  or or_3 (Salida[29], and_3_out, LC);
  and and_4 (and_4_out, Entrada[29], SRA1);
  and and_5 (and_5_out, Entrada[28], SRA1);
  or or_4 (Salida[28], and_4_out, LD);
  or or_5 (Salida[27], and_5_out, LE);
  and and_6 (and_6_out, Entrada[27], SRA1);
  and and_7 (and_7_out, Entrada[26], SRA1);
  or or_6 (Salida[26], and_6_out, LF);
  or or_7 (Salida[25], and_7_out, LG);
  and and_8 (and_8_out, Entrada[25], SRA1);
  and and_9 (and_9_out, Entrada[24], SRA1);
  or or_8 (Salida[24], and_8_out, LH);
  and and_10 (and_10_out, Entrada[23], SRA1);
  and and_11 (LA, Entrada[23], SLL8);
  or or_9 (Salida[23], and_9_out, LI);
  and and_12 (and_12_out, Entrada[22], SRA1);
  and and_13 (LB, Entrada[22], SLL8);
  or or_10 (Salida[22], and_10_out, LJ);
  and and_14 (LC, Entrada[21], SLL8);
  and and_15 (and_15_out, Entrada[21], SRA1);
  or or_11 (Salida[21], and_12_out, LK);
  and and_16 (LD, Entrada[20], SLL8);
  and and_17 (and_17_out, Entrada[20], SRA1);
  or or_12 (Salida[20], and_15_out, LL);
  and and_18 (and_18_out, Entrada[19], SRA1);
  and and_19 (LE, Entrada[19], SLL8);
  or or_13 (Salida[19], and_17_out, LM);
  and and_20 (and_20_out, Entrada[18], SRA1);
  and and_21 (LF, Entrada[18], SLL8);
  or or_14 (Salida[18], and_18_out, LN);
  and and_22 (and_22_out, Entrada[17], SRA1);
  and and_23 (LG, Entrada[17], SLL8);
  or or_15 (Salida[17], and_20_out, LO);
  and and_24 (and_24_out, Entrada[16], SRA1);
  and and_25 (LH, Entrada[16], SLL8);
  or or_16 (Salida[16], and_22_out, LP);
  and and_26 (LI, Entrada[15], SLL8);
  and and_27 (and_27_out, Entrada[15], SRA1);
  or or_17 (Salida[15], and_24_out, LQ);
  and and_28 (and_28_out, Entrada[14], SRA1);
  and and_29 (LJ, Entrada[14], SLL8);
  or or_18 (Salida[14], and_27_out, LR);
  and and_30 (and_30_out, Entrada[13], SRA1);
  and and_31 (LK, Entrada[13], SLL8);
  or or_19 (Salida[13], and_28_out, LS);
  and and_32 (LL, Entrada[12], SLL8);
  and and_33 (and_33_out, Entrada[12], SRA1);
  or or_20 (Salida[12], and_30_out, LT);
  and and_34 (LM, Entrada[11], SLL8);
  and and_35 (and_35_out, Entrada[11], SRA1);
  or or_21 (Salida[11], and_33_out, LU);
  and and_36 (LN, Entrada[10], SLL8);
  and and_37 (and_37_out, Entrada[10], SRA1);
  or or_22 (Salida[10], and_35_out, LV);
  and and_38 (and_38_out, Entrada[9], SRA1);
  and and_39 (LO, Entrada[9], SLL8);
  or or_23 (Salida[9], and_37_out, LW);
  and and_40 (LP, Entrada[8], SLL8);
  and and_41 (Salida[7], Entrada[8], SRA1);
  or or_24 (Salida[8], and_38_out, LX);
  and and_42 (Salida[6], Entrada[7], SRA1);
  and and_43 (LQ, Entrada[7], SLL8);
  and and_44 (Salida[5], Entrada[6], SRA1);
  and and_45 (LR, Entrada[6], SLL8);
  and and_46 (LS, Entrada[5], SLL8);
  and and_47 (Salida[4], Entrada[5], SRA1);
  and and_48 (Salida[3], Entrada[4], SRA1);
  and and_49 (LT, Entrada[4], SLL8);
  and and_50 (Salida[2], Entrada[3], SRA1);
  and and_51 (LU, Entrada[3], SLL8);
  and and_52 (Salida[1], Entrada[2], SRA1);
  and and_53 (LV, Entrada[2], SLL8);
  and and_54 (Salida[0], Entrada[1], SRA1);
  and and_55 (LW, Entrada[1], SLL8);
  and and_56 (LX, Entrada[0], SLL8);

  // Other names for the same wires on the sheet: E0 = Entrada[0]; E1 = Entrada[1]; E2 = Entrada[2]; E3 = Entrada[3];
  //   E4 = Entrada[4]; E5 = Entrada[5]; E6 = Entrada[6]; E7 = Entrada[7]; E8 = Entrada[8]; E9 = Entrada[9];
  //   E10 = Entrada[10]; E11 = Entrada[11]; E12 = Entrada[12]; E13 = Entrada[13]; E14 = Entrada[14];
  //   E15 = Entrada[15]; E16 = Entrada[16]; E17 = Entrada[17]; E18 = Entrada[18]; E19 = Entrada[19];
  //   E20 = Entrada[20]; E21 = Entrada[21]; E22 = Entrada[22]; E23 = Entrada[23]; E24 = Entrada[24];
  //   E25 = Entrada[25]; E26 = Entrada[26]; E27 = Entrada[27]; E28 = Entrada[28]; E29 = Entrada[29];
  //   E30 = Entrada[30]; E31 = Entrada[31]; S0 = Salida[0]; S1 = Salida[1]; S2 = Salida[2]; S3 = Salida[3];
  //   S4 = Salida[4]; S5 = Salida[5]; S6 = Salida[6]; S7 = Salida[7]; S8 = Salida[8]; S9 = Salida[9];
  //   S10 = Salida[10]; S11 = Salida[11]; S12 = Salida[12]; S13 = Salida[13]; S14 = Salida[14]; S15 = Salida[15];
  //   S16 = Salida[16]; S17 = Salida[17]; S18 = Salida[18]; S19 = Salida[19]; S20 = Salida[20]; S21 = Salida[21];
  //   S22 = Salida[22]; S23 = Salida[23]; S24 = Salida[24]; S25 = Salida[25]; S26 = Salida[26]; S27 = Salida[27];
  //   S28 = Salida[28]; S29 = Salida[29]; S30 = Salida[30]; S31 = Salida[31]
endmodule

module ALU_32_Bits (
  input  [31:0] A,
  input  CIN,
  input  ENB,
  input  ENA,
  input  INA,
  input  [31:0] B,
  input  [1:0] in_7,
  output [31:0] S,
  output COUT
);

  wire alu_8_bits_1_cout, alu_8_bits_2_cout, alu_8_bits_3_cout;

  ALU_8_bits alu_8_bits_1 (
    .A(A[31:24]), .B(B[31:24]), .F(in_7), .INVA(INA), .ENA(ENA), .ENB(ENB), .B_2(S[31:24]), .CIN(CIN),
    .COUT(alu_8_bits_1_cout));
  ALU_8_bits alu_8_bits_2 (
    .A(A[23:16]), .B(B[23:16]), .F(in_7), .INVA(INA), .ENA(ENA), .ENB(ENB), .B_2(S[23:16]),
    .CIN(alu_8_bits_1_cout), .COUT(alu_8_bits_2_cout));
  ALU_8_bits alu_8_bits_3 (
    .A(A[15:8]), .B(B[15:8]), .F(in_7), .INVA(INA), .ENA(ENA), .ENB(ENB), .B_2(S[15:8]),
    .CIN(alu_8_bits_2_cout), .COUT(alu_8_bits_3_cout));
  ALU_8_bits alu_8_bits_4 (
    .A(A[7:0]), .B(B[7:0]), .F(in_7), .INVA(INA), .ENA(ENA), .ENB(ENB), .B_2(S[7:0]),
    .CIN(alu_8_bits_3_cout), .COUT(COUT));

  // Other names for the same wires on the sheet: A0[7:0] = A[7:0]; A1[7:0] = A[15:8]; A2[7:0] = A[23:16];
  //   A3[7:0] = A[31:24]; B0[7:0] = B[7:0]; B1[7:0] = B[15:8]; B2[7:0] = B[23:16]; B3[7:0] = B[31:24]; F[1:0] = in_7
endmodule

module ALU_8_bits (
  input  [7:0] A,
  input  [7:0] B,
  input  CIN,
  input  [1:0] F,
  input  INVA,
  input  ENA,
  input  ENB,
  output [7:0] B_2,
  output COUT
);

  wire alu_1_bit_1_cout, alu_1_bit_2_cout, alu_1_bit_3_cout, alu_1_bit_4_cout, alu_1_bit_5_cout,
       alu_1_bit_6_cout, alu_1_bit_7_cout;

  ALU_1_bit alu_1_bit_1 (
    .F(F), .Salida(B_2[7]), .Cin(CIN), .Cout(alu_1_bit_1_cout), .INVA(INVA), .A(A[7]), .ENA(ENA), .B(B[7]),
    .ENB(ENB));
  ALU_1_bit alu_1_bit_2 (
    .F(F), .Salida(B_2[6]), .Cin(alu_1_bit_1_cout), .Cout(alu_1_bit_2_cout), .INVA(INVA), .A(A[6]),
    .ENA(ENA), .B(B[6]), .ENB(ENB));
  ALU_1_bit alu_1_bit_3 (
    .F(F), .Salida(B_2[5]), .Cin(alu_1_bit_2_cout), .Cout(alu_1_bit_3_cout), .INVA(INVA), .A(A[5]),
    .ENA(ENA), .B(B[5]), .ENB(ENB));
  ALU_1_bit alu_1_bit_4 (
    .F(F), .Salida(B_2[4]), .Cin(alu_1_bit_3_cout), .Cout(alu_1_bit_4_cout), .INVA(INVA), .A(A[4]),
    .ENA(ENA), .B(B[4]), .ENB(ENB));
  ALU_1_bit alu_1_bit_5 (
    .F(F), .Salida(B_2[3]), .Cin(alu_1_bit_4_cout), .Cout(alu_1_bit_5_cout), .INVA(INVA), .A(A[3]),
    .ENA(ENA), .B(B[3]), .ENB(ENB));
  ALU_1_bit alu_1_bit_6 (
    .F(F), .Salida(B_2[2]), .Cin(alu_1_bit_5_cout), .Cout(alu_1_bit_6_cout), .INVA(INVA), .A(A[2]),
    .ENA(ENA), .B(B[2]), .ENB(ENB));
  ALU_1_bit alu_1_bit_7 (
    .F(F), .Salida(B_2[1]), .Cin(alu_1_bit_6_cout), .Cout(alu_1_bit_7_cout), .INVA(INVA), .A(A[1]),
    .ENA(ENA), .B(B[1]), .ENB(ENB));
  ALU_1_bit alu_1_bit_8 (
    .F(F), .Salida(B_2[0]), .Cin(alu_1_bit_7_cout), .Cout(COUT), .INVA(INVA), .A(A[0]), .ENA(ENA), .B(B[0]),
    .ENB(ENB));
endmodule

module MAR (
  input  [31:0] Entrada,
  input  ENA,
  input  CLK,
  input  CLEAR,
  output [31:0] Salida
);

  Register #(.width(32)) register_1 (.D(Entrada), .en(ENA), .Q(Salida), .clk(CLK), .clr(CLEAR));
endmodule

module MDR (
  input  [31:0] Entrada,
  input  ENA,
  input  CLK,
  input  CLEAR,
  output [31:0] Salida
);

  Register #(.width(32)) register_1 (.D(Entrada), .en(ENA), .Q(Salida), .clk(CLK), .clr(CLEAR));
endmodule

module ZN (
  input  [31:0] in_1,
  output Z,
  output N
);

  wire or_1_out;

  or or_1 (or_1_out, in_1[0], in_1[1], in_1[2], in_1[3], in_1[4], in_1[5], in_1[6], in_1[7], in_1[8], in_1[9], in_1[10], in_1[11], in_1[12], in_1[13], in_1[14], in_1[15], in_1[17], in_1[18], in_1[19], in_1[20], in_1[21], in_1[22], in_1[23], in_1[24], in_1[25], in_1[26], in_1[27], in_1[28], in_1[29], in_1[30], in_1[31], in_1[16]);
  not not_1 (Z, or_1_out);

  assign N = in_1[31];
endmodule
